// Logisim project CPU.circ as structural Verilog: 4 circuits, main circuit main
module main (
);

  wire button_1_out, button_2_out, clock_1_out, cpu_1__0, cpu_1__1, cpu_1__2, cpu_1__3;
  wire [15:0] cpu_1_output_0, cpu_1_output_1, cpu_1_output_2, cpu_1_output_3, register_1_q, register_2_q,
       register_3_q, register_4_q;

  Clock clock_1 (.out(clock_1_out));
  CPU cpu_1 (
    .CLOCK(clock_1_out), .START(button_1_out), .STOP(button_2_out), ._0(cpu_1__0), ._1(cpu_1__1),
    ._2(cpu_1__2), ._3(cpu_1__3), .OUTPUT_0(cpu_1_output_0), .OUTPUT_1(cpu_1_output_1),
    .OUTPUT_2(cpu_1_output_2), .OUTPUT_3(cpu_1_output_3));  // open: INPUT_0_2, INPUT_1_2, INPUT_2_2, INPUT_3_2, INPUT_0, INPUT_1, INPUT_2, INPUT_3
  Button button_1 (.out(button_1_out));
  Button button_2 (.out(button_2_out));
  Register #(.width(16), .trigger("high")) register_1 (
    .D(cpu_1_output_0), .Q(register_1_q), .clk(cpu_1__0));  // open: en, clr
  Register #(.width(16), .trigger("high")) register_2 (
    .D(cpu_1_output_1), .Q(register_2_q), .clk(cpu_1__1));  // open: en, clr
  // Probe on register_1_q
  // Probe on register_2_q
  Register #(.width(16), .trigger("high")) register_3 (
    .D(cpu_1_output_2), .Q(register_3_q), .clk(cpu_1__2));  // open: en, clr
  // Probe on register_3_q
  Register #(.width(16), .trigger("high")) register_4 (
    .D(cpu_1_output_3), .Q(register_4_q), .clk(cpu_1__3));  // open: en, clr
  // Probe on register_4_q
endmodule

module CPU (
  input  CLOCK,
  input  START,
  input  STOP,
  input  INPUT_0,
  input  INPUT_1,
  input  INPUT_2,
  input  INPUT_3,
  input  [15:0] INPUT_0_2,
  input  [15:0] INPUT_1_2,
  input  [15:0] INPUT_2_2,
  input  [15:0] INPUT_3_2,
  output _0,
  output _1,
  output _2,
  output _3,
  output [15:0] OUTPUT_0,
  output [15:0] OUTPUT_1,
  output [15:0] OUTPUT_2,
  output [15:0] OUTPUT_3
);

  wire and_1_out, and_2_out, comparator_1_eq, comparator_1_gt, comparator_1_lt, decoder_1_out0,
       decoder_1_out1, decoder_1_out2, decoder_1_out3, decoder_1_out4, decoder_1_out5, decoder_2_out0,
       decoder_2_out1, decoder_2_out2, decoder_2_out3, decoder_2_out4, decoder_2_out5, decoder_2_out6,
       decoder_2_out7, decoder_2_out8, decoder_2_out9, multiplexer_7_out, multiplexer_8_out, not_1_out,
       not_2_out, or_1_out, or_2_out, priority_encoder_1_gs, priority_encoder_2_gs, priority_encoder_3_p4,
       priority_encoder_4_gs, priority_encoder_5_gs, t_ff_1_q, t_ff_1_qn;
  wire [1:0] priority_encoder_2_out, priority_encoder_3_p3, priority_encoder_4_out, priority_encoder_5_out,
       rom_1_data_2;
  wire [2:0] priority_encoder_1_out;
  wire [15:0] alu_1_result, counter_1_q, multiplexer_1_out, multiplexer_2_out, multiplexer_3_out,
       multiplexer_4_out, multiplexer_5_out, multiplexer_6_out, ram_1_data, register_file_1_out_data_1,
       register_file_1_out_data_2, register_file_1_out_data_3;
  wire [31:0] rom_1_data;

  not not_1 (not_1_out, priority_encoder_4_gs);
  and and_1 (and_1_out, CLOCK, t_ff_1_q);
  T_Flip_Flop t_ff_1 (.Q(t_ff_1_q), .Qn(t_ff_1_qn), .preset(START), .reset(STOP));  // open: clk, T, en
  Counter #(.width(16), .max('hffff)) counter_1 (
    .load(priority_encoder_4_gs), .D(multiplexer_6_out), .count(not_1_out), .Q(counter_1_q), .clk(and_1_out),
    .clr(t_ff_1_qn));  // open: carry
  Multiplexer #(.select(2), .width(16), .disabled(0), .enable("false")) multiplexer_1 (
    .in0(INPUT_0_2), .in1(INPUT_1_2), .in2(INPUT_2_2), .in3(INPUT_3_2), .out(multiplexer_1_out),
    .sel(rom_1_data_2));
  Multiplexer #(.select(3), .width(16)) multiplexer_2 (
    .in0(register_file_1_out_data_1), .in1(rom_1_data[15:0]), .in2(ram_1_data), .in3(multiplexer_1_out),
    .in4(alu_1_result), .out(multiplexer_2_out), .sel(priority_encoder_1_out), .en(priority_encoder_1_gs));  // open: in5, in6, in7
  Priority_Encoder priority_encoder_1 (
    .in0(decoder_2_out0), .in1(decoder_2_out1), .in2(decoder_2_out2), .in3(decoder_2_out3),
    .in4(priority_encoder_3_p4), .out(priority_encoder_1_out), .gs(priority_encoder_1_gs));  // open: in5, in6, in7, en_in, en_out
  ROM #(.addrWidth(16), .dataWidth(32)) rom_1 (
    .addr(counter_1_q), .data({rom_1_data[31:24], rom_1_data_2, rom_1_data[21:0]}));  // open: sel
  REGISTER_FILE register_file_1 (
    .REG_NO(rom_1_data[17:16]), .CLOCK(and_1_out), .OUT_REG_2(rom_1_data[19:18]),
    .OUT_REG_1(rom_1_data[21:20]), .DATA(multiplexer_2_out), .WRITE(priority_encoder_1_gs),
    .OUT_DATA_1(register_file_1_out_data_1), .OUT_DATA_2(register_file_1_out_data_2),
    .OUT_DATA_3(register_file_1_out_data_3), .OUT_REG_3(rom_1_data_2));
  Multiplexer #(.select(2), .width(16)) multiplexer_3 (
    .in0(register_file_1_out_data_1), .in1(rom_1_data[15:0]), .out(multiplexer_3_out),
    .sel(priority_encoder_3_p3), .en(priority_encoder_3_p4));  // open: in2, in3
  ALU alu_1 (
    .CLOCK(and_1_out), .UPDATE(rom_1_data_2[1]), .OPERATOR_NO(rom_1_data[27:24]), .A(multiplexer_3_out),
    .B(register_file_1_out_data_2), .RESULT(alu_1_result));
  Decoder #(.select(4), .disabled(0), .enable("false")) decoder_1 (
    .out0(decoder_1_out0), .out1(decoder_1_out1), .out2(decoder_1_out2), .out3(decoder_1_out3),
    .out4(decoder_1_out4), .out5(decoder_1_out5), .sel(rom_1_data[31:28]));  // open: out6, out7, out8, out9, out10, out11, out12, out13, out14, out15
  Priority_Encoder #(.select(2)) priority_encoder_2 (
    .in0(decoder_2_out4), .in1(decoder_2_out5), .in2(decoder_2_out6), .out(priority_encoder_2_out),
    .gs(priority_encoder_2_gs));  // open: in3, en_out, en_in
  // Priority_Encoder #(.select(2), .disabled(0)) priority_encoder_3: pin names not known; wires that end beside it: decoder_1_out4, decoder_1_out5, priority_encoder_3_p3, priority_encoder_3_p4
  Decoder #(.select(4), .disabled(0)) decoder_2 (
    .out0(decoder_2_out0), .out1(decoder_2_out1), .out2(decoder_2_out2), .out3(decoder_2_out3),
    .out4(decoder_2_out4), .out5(decoder_2_out5), .out6(decoder_2_out6), .out7(decoder_2_out7),
    .out8(decoder_2_out8), .out9(decoder_2_out9), .sel(rom_1_data[27:24]), .en(decoder_1_out0));  // open: out10, out11, out12, out13, out14, out15
  Multiplexer #(.select(2), .width(16)) multiplexer_4 (
    .in0(register_file_1_out_data_1), .in1(rom_1_data[15:0]), .in2(multiplexer_1_out),
    .out(multiplexer_4_out), .sel(priority_encoder_2_out), .en(priority_encoder_2_gs));  // open: in3
  RAM #(.addrWidth(16), .dataWidth(16), .bus("separate")) ram_1 (
    .addr(register_file_1_out_data_2), .din(multiplexer_4_out), .data(ram_1_data),
    .str(priority_encoder_2_gs), .clk(and_1_out), .ld(1'b1));  // open: sel, clr
  Priority_Encoder #(.select(2)) priority_encoder_4 (
    .in0(decoder_1_out1), .in1(decoder_1_out2), .in2(decoder_1_out3), .out(priority_encoder_4_out),
    .gs(priority_encoder_4_gs), .en_in(multiplexer_8_out));  // open: in3, en_out
  Multiplexer #(.select(2), .width(16)) multiplexer_5 (
    .in0(register_file_1_out_data_1), .in1(rom_1_data[15:0]), .in2(ram_1_data), .out(multiplexer_5_out),
    .sel(priority_encoder_5_out), .en(priority_encoder_5_gs));  // open: in3
  Priority_Encoder #(.select(2)) priority_encoder_5 (
    .in0(decoder_2_out7), .in1(decoder_2_out8), .in2(decoder_2_out9), .out(priority_encoder_5_out),
    .gs(priority_encoder_5_gs));  // open: in3, en_out, en_in
  and and_2 (and_2_out, and_1_out, priority_encoder_5_gs);
  Multiplexer #(.select(2), .width(16)) multiplexer_6 (
    .in0(register_file_1_out_data_1), .in1(rom_1_data[15:0]), .in2(ram_1_data), .out(multiplexer_6_out),
    .sel(priority_encoder_4_out), .en(priority_encoder_4_gs));  // open: in3
  Decoder #(.select(2), .disabled(0)) decoder_3 (
    .out0(_0), .out1(_1), .out2(_2), .out3(_3), .sel(rom_1_data_2), .en(and_2_out));
  Demultiplexer #(.select(2), .width(16), .tristate("true")) demultiplexer_1 (
    .out0(OUTPUT_0), .out1(OUTPUT_1), .out2(OUTPUT_2), .out3(OUTPUT_3), .in(multiplexer_5_out),
    .sel(rom_1_data_2), .en(and_2_out));
  Comparator #(.width(16)) comparator_1 (
    .a(register_file_1_out_data_3), .b({16{1'b0}}), .gt(comparator_1_gt), .eq(comparator_1_eq),
    .lt(comparator_1_lt));
  or or_1 (or_1_out, comparator_1_lt, comparator_1_eq);
  not not_2 (not_2_out, multiplexer_7_out);
  or or_2 (or_2_out, comparator_1_gt, comparator_1_eq);
  Multiplexer #(.select(2), .disabled(0), .enable("false")) multiplexer_7 (
    .in0(INPUT_0), .in1(INPUT_1), .in2(INPUT_2), .in3(INPUT_3), .out(multiplexer_7_out), .sel(rom_1_data_2));
  Pull_Resistor pull_resistor_1 (.node(multiplexer_7_out));
  Multiplexer #(.select(4), .disabled(0), .enable("false")) multiplexer_8 (
    .in0(1'b1), .in1(comparator_1_lt), .in2(or_1_out), .in3(comparator_1_eq), .in4(or_2_out),
    .in5(comparator_1_gt), .in6(multiplexer_7_out), .in7(not_2_out), .out(multiplexer_8_out),
    .sel(rom_1_data[27:24]));  // open: in8, in9, in10, in11, in12, in13, in14, in15

  // Notes on the sheet:
  //   contents of rom_1 (hex, n*v repeats v):
  //   1000000 5000000 50000001 5000000 50000001 5000000 50000001 5000000 50000001 5000000 50000001 5000000
  //   50000001 5000000 50000001 5000001 1020000 2080000 7000000 1020001 2080000 7400000 1020002 2080000
  //   7800000 1020003 2080000 7c00000 1020003 2080000 1020007 2090000 40900000 4080000 1020003 4180000
  //   1020002 2080000 1020006 2090000 41900000 4080000 1020002 4180000 1020001 2080000 1020005 2090000
  //   41900000 4080000 1020001 4180000 1020000 2080000 1020004 2090000 41900000 4080000 1020000 4180000
  //   20000010
endmodule

module REGISTER_FILE (
  input  [1:0] REG_NO,
  input  CLOCK,
  input  [1:0] OUT_REG_2,
  input  [1:0] OUT_REG_1,
  input  [1:0] OUT_REG_3,
  input  [15:0] DATA,
  input  WRITE,
  output [15:0] OUT_DATA_1,
  output [15:0] OUT_DATA_2,
  output [15:0] OUT_DATA_3
);

  wire decoder_1_out0, decoder_1_out1, decoder_1_out2, decoder_1_out3;
  wire [15:0] register_1_q, register_2_q, register_3_q, register_4_q;

  Decoder #(.select(2), .disabled(0)) decoder_1 (
    .out0(decoder_1_out0), .out1(decoder_1_out1), .out2(decoder_1_out2), .out3(decoder_1_out3), .sel(REG_NO),
    .en(WRITE));
  Multiplexer #(.select(2), .width(16), .enable("false")) multiplexer_1 (
    .in0(register_1_q), .in1(register_2_q), .in2(register_3_q), .in3(register_4_q), .out(OUT_DATA_1),
    .sel(OUT_REG_1));
  Register #(.width(16)) register_1 (.D(DATA), .en(decoder_1_out0), .Q(register_1_q), .clk(CLOCK));  // open: clr
  Register #(.width(16)) register_2 (.D(DATA), .en(decoder_1_out1), .Q(register_2_q), .clk(CLOCK));  // open: clr
  Register #(.width(16)) register_3 (.D(DATA), .en(decoder_1_out2), .Q(register_3_q), .clk(CLOCK));  // open: clr
  Register #(.width(16)) register_4 (.D(DATA), .en(decoder_1_out3), .Q(register_4_q), .clk(CLOCK));  // open: clr
  Multiplexer #(.select(2), .width(16), .enable("false")) multiplexer_2 (
    .in0(register_1_q), .in1(register_2_q), .in2(register_3_q), .in3(register_4_q), .out(OUT_DATA_2),
    .sel(OUT_REG_2));
  Multiplexer #(.select(2), .width(16), .enable("false")) multiplexer_3 (
    .in0(register_1_q), .in1(register_2_q), .in2(register_3_q), .in3(register_4_q), .out(OUT_DATA_3),
    .sel(OUT_REG_3));
endmodule

module ALU (
  input  CLOCK,
  input  UPDATE,
  input  [3:0] OPERATOR_NO,
  input  [15:0] A,
  input  [15:0] B,
  output [15:0] RESULT
);

  wire [1:0] adder_2_cout, register_1_q;
  wire [3:0] bit_extender_1_out;
  wire [15:0] adder_1_out, adder_2_out, and_1_out, divider_1_out, divider_1_rem, multiplier_1_cout,
       multiplier_1_out, or_1_out, shifter_1_out, shifter_2_out, shifter_3_out, subtractor_1_out,
       subtractor_2_out, xor_1_out;

  Adder #(.width(16)) adder_1 (.a(A), .b(B), .out(adder_1_out));  // open: cin, cout
  Adder #(.width(16)) adder_2 (.a(A), .b(B), .out(adder_2_out), .cin(register_1_q[1]), .cout(adder_2_cout[0]));
  Subtractor #(.width(16)) subtractor_1 (.a(A), .b(B), .out(subtractor_1_out));  // open: bin, bout
  Subtractor #(.width(16)) subtractor_2 (
    .a(A), .b(B), .out(subtractor_2_out), .bin(register_1_q[0]), .bout(adder_2_cout[1]));
  Multiplier #(.width(16)) multiplier_1 (.a(A), .b(B), .out(multiplier_1_out), .cout(multiplier_1_cout));  // open: cin
  Divider #(.width(16)) divider_1 (.a(A), .b(B), .out(divider_1_out), .rem(divider_1_rem));  // open: upper
  assign and_1_out = A & B;  // AND_Gate and_1, 16 bits wide
  assign or_1_out = A | B;  // OR_Gate or_1, 16 bits wide
  assign xor_1_out = A ^ B;  // XOR_Gate xor_1, 16 bits wide
  Bit_Extender #(.in_width(16), .out_width(4)) bit_extender_1 (.in(B), .out(bit_extender_1_out));
  Register #(.width(2)) register_1 (.D(adder_2_cout), .en(UPDATE), .Q(register_1_q), .clk(CLOCK));  // open: clr
  Shifter #(.width(16), .shift("ar")) shifter_1 (.in(A), .\dist (bit_extender_1_out), .out(shifter_1_out));
  Shifter #(.width(16), .shift("rl")) shifter_2 (.in(A), .\dist (bit_extender_1_out), .out(shifter_2_out));
  Shifter #(.width(16), .shift("rr")) shifter_3 (.in(A), .\dist (bit_extender_1_out), .out(shifter_3_out));
  Multiplexer #(.select(4), .width(16), .disabled(0), .enable("false")) multiplexer_1 (
    .in0(adder_1_out), .in1(adder_2_out), .in2(subtractor_1_out), .in3(subtractor_2_out),
    .in4(multiplier_1_out), .in5(multiplier_1_cout), .in6(divider_1_out), .in7(divider_1_rem),
    .in8(and_1_out), .in9(or_1_out), .in10(xor_1_out), .in11(shifter_1_out), .in12(shifter_2_out),
    .in13(shifter_3_out), .out(RESULT), .sel(OPERATOR_NO));  // open: in14, in15
endmodule
